// Logisim project Basic-Computer.circ as structural Verilog: 30 circuits, main circuit main
module main (
  output [2:0] out_1,
  output [15:0] out_2,
  output [15:0] out_3,
  output [15:0] out_4,
  output [15:0] out_5,
  output [15:0] out_6,
  output [15:0] out_7,
  output [15:0] out_8,
  output [7:0] out_9
);

  wire Clock, clock_1_out, CLR_AC, CLR_AR, CLR_PC, E, E_OUT, FGI, FGO, I, IEN, INR_AC, INR_AR, INR_DR,
       INR_PC, LD_AC, LD_AR, LD_DR, LD_IR, LD_OUTR, LD_PC, LD_TR, not_1_out, not_2_out, R, read, S,
       sc_control_1_clr_sc, write;
  wire [3:0] SC;
  wire [6:0] CTRL;
  wire [7:0] INPR;
  wire [15:0] n16_bit_alu_1_result, ram_1_data, tr_1_output;

  Clock clock_1 (.out(clock_1_out));
  not not_1 (not_1_out, S);
  R r_1 (.FGO(FGO), .FGI(FGI), .IEN(IEN), .in_5(SC), .R(R), .Clock(Clock));
  IEN ien_1 (.Clock(Clock), .T(SC), .R(R), .IR(out_8), .I(I), .IEN(IEN));
  and and_1 (Clock, clock_1_out, not_1_out);
  MEMORY_control memory_control_1 (.T(SC), .R(R), .I(I), .IR(out_8), .WR_MEMORY(write), .RD_MEMORY(read));
  PC_control pc_control_1 (
    .T(SC), .IR(out_8), .I(I), .R(R), .E(E), .FGI(FGI), .FGO(FGO), .INR_PC(INR_PC), .CLR_PC(CLR_PC),
    .LD_PC(LD_PC), .AC(out_7), .DR(out_6));
  _16_bit_ALU u_16_bit_alu_1 (
    .INPR(INPR), .DR(out_6), .AC(out_7), .result(n16_bit_alu_1_result), .E_IN(E), .AND(CTRL[0]),
    .ADD(CTRL[1]), .DR_2(CTRL[2]), .INPR_2(CTRL[3]), .COM(CTRL[4]), .SLR(CTRL[5]), .SHL(CTRL[6]),
    .Carry_E(E_OUT));
  IR_control ir_control_1 (.T(SC), .R(R), .LD_IR(LD_IR));
  OUTR outr_1 (.INPUT(out_3), .OUTPUT(out_9), .Clock(Clock), .LD_OUTR(LD_OUTR));
  BUS_control bus_control_1 (.T(SC), .R(R), .I(I), .IR(out_8), .Select(out_1));
  S s_1 (.T(SC), .IR(out_8), .I(I), .S(S), .Clock(Clock));
  AR_control ar_control_1 (.T(SC), .R(R), .IR(out_8), .LD_AR(LD_AR), .CLR_AR(CLR_AR), .INR_AR(INR_AR), .I(I));
  DR_control dr_control_1 (.T(SC), .R(R), .I(I), .IR(out_8), .LD_DR(LD_DR), .INR_DR(INR_DR));
  I i_1 (.Clock(Clock), .IR_15(out_8[15]), .T(SC), .R(R), .I(I));
  FGI fgi_1 (.T(SC), .I(I), .IR(out_8), .INPR(INPR), .FGI(FGI), .Clock(Clock));
  FGO fgo_1 (.T(SC), .I(I), .IR(out_8), .FGO(FGO), .Clock(Clock));
  AC_control ac_control_1 (.T(SC), .I(I), .IR(out_8), .LD_AC(LD_AC), .CTRL(CTRL), .INR_AC(INR_AC), .CLR_AC(CLR_AC));
  IR ir_1 (.INPUT(out_3), .OUTPUT(out_8), .Clock(Clock), .LD_IR(LD_IR));
  OUTR_control outr_control_1 (.T(SC), .IR(out_8), .I(I), .LD_OUTR(LD_OUTR));
  AR ar_1 (.INPUT(out_3), .OUTPUT(out_2), .CLR_AR(CLR_AR), .Clock(Clock), .LD_AR(LD_AR), .INR_AR(INR_AR));
  DR dr_1 (.INPUT(out_3), .OUTPUT(out_6), .Clock(Clock), .LD_DR(LD_DR), .INR_DR(INR_DR));  // open: CLR_DR
  TR_control tr_control_1 (.T(SC), .R(R), .LD_TR(LD_TR));
  E e_1 (.T(SC), .R(R), .I(I), .IR(out_8), .in_2(E_OUT), .E(E), .Clock(Clock));
  SC_control sc_control_1 (.T(SC), .R(R), .I(I), .IR(out_8), .CLR_SC(sc_control_1_clr_sc));
  PC pc_1 (.INPUT(out_3), .OUTPUT(out_4), .CLR_PC(CLR_PC), .Clock(Clock), .LD_PC(LD_PC), .INR_PC(INR_PC));
  AC ac_1 (
    .INPUT(n16_bit_alu_1_result), .OUTPUT(out_7), .CLR_AC(CLR_AC), .Clock(Clock), .LD_AC(LD_AC),
    .INR_AC(INR_AC));
  not not_2 (not_2_out, sc_control_1_clr_sc);
  RAM #(.addrWidth(12), .dataWidth(16), .bus("separate")) ram_1 (
    .addr(out_2[11:0]), .din(out_3), .data(ram_1_data), .str(write), .clk(Clock), .ld(read));  // open: sel, clr
  INPR inpr_1 (.out_1(INPR));
  TR tr_1 (.INPUT(out_3), .OUTPUT(tr_1_output), .Clock(Clock), .LD_TR(LD_TR));  // open: CLR_TR
  Counter #(.width(4), .max('hf)) counter_1 (
    .load(sc_control_1_clr_sc), .D(4'b0000), .count(not_2_out), .Q(SC), .clk(Clock));  // open: carry, clr
  BUS bus_1 (
    .AR(out_2), .PC(out_4), .DR(out_6), .AC(out_7), .IR(out_8), .TR(tr_1_output), .MEMORY(ram_1_data),
    .out_10(out_3), .in_7(out_1));  // open: NULL

  assign out_5 = out_3;

  // Other names for the same wires on the sheet: AC[15:0] = out_7; DR[15:0] = out_6; IR[15:0] = out_8;
  //   IR_15 = out_8[15]; AR[11:0] = out_2[11:0]; Select[2:0] = out_1
endmodule

module Full_Adder (
  input  x,
  input  y,
  input  z,
  output S,
  output C
);

  wire and_1_out, and_2_out, xor_1_out;

  xor xor_1 (xor_1_out, x, y);
  and and_1 (and_1_out, x, y);
  xor xor_2 (S, xor_1_out, z);
  and and_2 (and_2_out, xor_1_out, z);
  or or_1 (C, and_2_out, and_1_out);
endmodule

module _1_bit_ALU (
  input  [6:0] in_1,
  input  INPR_i,
  input  DR_i,
  input  AC_i,
  input  AC_i_1,
  input  AC_i_1_2,
  input  C_i,
  output C_i_1,
  output I_i
);

  wire and_1_out, and_2_out, and_3_out, and_4_out, and_5_out, and_6_out, and_7_out, full_adder_1_s, not_1_out;

  Full_Adder full_adder_1 (.x(C_i), .y(AC_i), .z(DR_i), .C(C_i_1), .S(full_adder_1_s));
  not not_1 (not_1_out, AC_i);
  and and_1 (and_1_out, AC_i, DR_i, in_1[6]);
  and and_2 (and_2_out, in_1[5], full_adder_1_s);
  and and_3 (and_3_out, in_1[4], DR_i);
  and and_4 (and_4_out, in_1[3], INPR_i);
  and and_5 (and_5_out, in_1[2], not_1_out);
  and and_6 (and_6_out, in_1[1], AC_i_1_2);
  and and_7 (and_7_out, in_1[0], AC_i_1);
  or or_1 (I_i, and_1_out, and_2_out, and_3_out, and_4_out, and_5_out, and_6_out, and_7_out);
endmodule

module _16_bit_ALU (
  input  [7:0] INPR,
  input  [15:0] DR,
  input  E_IN,
  input  [15:0] AC,
  input  SLR,
  input  COM,
  input  INPR_2,
  input  SHL,
  input  DR_2,
  input  ADD,
  input  AND,
  output [15:0] result,
  output Carry_E
);

  wire and_1_out, and_2_out, and_3_out, and_4_out, Carry_E_t, n1_bit_alu_1_c_i_1, n1_bit_alu_2_c_i_1,
       n1_bit_alu_3_c_i_1, n1_bit_alu_4_c_i_1, n1_bit_alu_5_c_i_1, n1_bit_alu_6_c_i_1, n1_bit_alu_7_c_i_1,
       n1_bit_alu_8_c_i_1, n1_bit_alu_9_c_i_1, n1_bit_alu_10_c_i_1, n1_bit_alu_11_c_i_1, n1_bit_alu_12_c_i_1,
       n1_bit_alu_13_c_i_1, n1_bit_alu_14_c_i_1, n1_bit_alu_15_c_i_1, not_1_out, or_1_out;

  and and_1 (and_1_out, Carry_E_t, ADD);
  and and_2 (and_2_out, SLR, AC[0]);
  and and_3 (and_3_out, SHL, AC[15]);
  not not_1 (not_1_out, or_1_out);
  or or_1 (or_1_out, SHL, SLR, ADD);
  and and_4 (and_4_out, E_IN, not_1_out);
  or or_2 (Carry_E, and_1_out, and_2_out, and_3_out, and_4_out);
  _1_bit_ALU u_1_bit_alu_1 (
    .C_i_1(n1_bit_alu_1_c_i_1), .I_i(result[0]), .INPR_i(INPR[0]), .DR_i(DR[0]), .AC_i(AC[0]), .AC_i_1(E_IN),
    .AC_i_1_2(AC[1]), .C_i(1'b0), .in_1({AND, ADD, DR_2, INPR_2, COM, SLR, SHL}));
  _1_bit_ALU u_1_bit_alu_2 (
    .C_i_1(n1_bit_alu_2_c_i_1), .I_i(result[1]), .INPR_i(INPR[1]), .DR_i(DR[1]), .AC_i(AC[1]),
    .AC_i_1(AC[0]), .AC_i_1_2(AC[2]), .C_i(n1_bit_alu_1_c_i_1), .in_1({AND, ADD, DR_2, INPR_2, COM, SLR, SHL}));
  _1_bit_ALU u_1_bit_alu_3 (
    .C_i_1(n1_bit_alu_3_c_i_1), .I_i(result[2]), .INPR_i(INPR[2]), .DR_i(DR[2]), .AC_i(AC[2]),
    .AC_i_1(AC[1]), .AC_i_1_2(AC[3]), .C_i(n1_bit_alu_2_c_i_1), .in_1({AND, ADD, DR_2, INPR_2, COM, SLR, SHL}));
  _1_bit_ALU u_1_bit_alu_4 (
    .C_i_1(n1_bit_alu_4_c_i_1), .I_i(result[3]), .INPR_i(INPR[3]), .DR_i(DR[3]), .AC_i(AC[3]),
    .AC_i_1(AC[2]), .AC_i_1_2(AC[4]), .C_i(n1_bit_alu_3_c_i_1), .in_1({AND, ADD, DR_2, INPR_2, COM, SLR, SHL}));
  _1_bit_ALU u_1_bit_alu_5 (
    .C_i_1(n1_bit_alu_5_c_i_1), .I_i(result[4]), .INPR_i(INPR[4]), .DR_i(DR[4]), .AC_i(AC[4]),
    .AC_i_1(AC[3]), .AC_i_1_2(AC[5]), .C_i(n1_bit_alu_4_c_i_1), .in_1({AND, ADD, DR_2, INPR_2, COM, SLR, SHL}));
  _1_bit_ALU u_1_bit_alu_6 (
    .C_i_1(n1_bit_alu_6_c_i_1), .I_i(result[5]), .INPR_i(INPR[5]), .DR_i(DR[5]), .AC_i(AC[5]),
    .AC_i_1(AC[4]), .AC_i_1_2(AC[6]), .C_i(n1_bit_alu_5_c_i_1), .in_1({AND, ADD, DR_2, INPR_2, COM, SLR, SHL}));
  _1_bit_ALU u_1_bit_alu_7 (
    .C_i_1(n1_bit_alu_7_c_i_1), .I_i(result[6]), .INPR_i(INPR[6]), .DR_i(DR[6]), .AC_i(AC[6]),
    .AC_i_1(AC[5]), .AC_i_1_2(AC[7]), .C_i(n1_bit_alu_6_c_i_1), .in_1({AND, ADD, DR_2, INPR_2, COM, SLR, SHL}));
  _1_bit_ALU u_1_bit_alu_8 (
    .C_i_1(n1_bit_alu_8_c_i_1), .I_i(result[7]), .INPR_i(INPR[7]), .DR_i(DR[7]), .AC_i(AC[7]),
    .AC_i_1(AC[6]), .AC_i_1_2(AC[8]), .C_i(n1_bit_alu_7_c_i_1), .in_1({AND, ADD, DR_2, INPR_2, COM, SLR, SHL}));
  _1_bit_ALU u_1_bit_alu_9 (
    .C_i_1(n1_bit_alu_9_c_i_1), .I_i(result[8]), .INPR_i(1'b0), .DR_i(DR[8]), .AC_i(AC[8]), .AC_i_1(AC[7]),
    .AC_i_1_2(AC[9]), .C_i(n1_bit_alu_8_c_i_1), .in_1({AND, ADD, DR_2, INPR_2, COM, SLR, SHL}));
  _1_bit_ALU u_1_bit_alu_10 (
    .C_i_1(n1_bit_alu_10_c_i_1), .I_i(result[9]), .INPR_i(1'b0), .DR_i(DR[9]), .AC_i(AC[9]), .AC_i_1(AC[8]),
    .AC_i_1_2(AC[10]), .C_i(n1_bit_alu_9_c_i_1), .in_1({AND, ADD, DR_2, INPR_2, COM, SLR, SHL}));
  _1_bit_ALU u_1_bit_alu_11 (
    .C_i_1(n1_bit_alu_11_c_i_1), .I_i(result[10]), .INPR_i(1'b0), .DR_i(DR[10]), .AC_i(AC[10]),
    .AC_i_1(AC[9]), .AC_i_1_2(AC[11]), .C_i(n1_bit_alu_10_c_i_1),
    .in_1({AND, ADD, DR_2, INPR_2, COM, SLR, SHL}));
  _1_bit_ALU u_1_bit_alu_12 (
    .C_i_1(n1_bit_alu_12_c_i_1), .I_i(result[11]), .INPR_i(1'b0), .DR_i(DR[11]), .AC_i(AC[11]),
    .AC_i_1(AC[10]), .AC_i_1_2(AC[12]), .C_i(n1_bit_alu_11_c_i_1),
    .in_1({AND, ADD, DR_2, INPR_2, COM, SLR, SHL}));
  _1_bit_ALU u_1_bit_alu_13 (
    .C_i_1(n1_bit_alu_13_c_i_1), .I_i(result[12]), .INPR_i(1'b0), .DR_i(DR[12]), .AC_i(AC[12]),
    .AC_i_1(AC[11]), .AC_i_1_2(AC[13]), .C_i(n1_bit_alu_12_c_i_1),
    .in_1({AND, ADD, DR_2, INPR_2, COM, SLR, SHL}));
  _1_bit_ALU u_1_bit_alu_14 (
    .C_i_1(n1_bit_alu_14_c_i_1), .I_i(result[13]), .INPR_i(1'b0), .DR_i(DR[13]), .AC_i(AC[13]),
    .AC_i_1(AC[12]), .AC_i_1_2(AC[14]), .C_i(n1_bit_alu_13_c_i_1),
    .in_1({AND, ADD, DR_2, INPR_2, COM, SLR, SHL}));
  _1_bit_ALU u_1_bit_alu_15 (
    .C_i_1(n1_bit_alu_15_c_i_1), .I_i(result[14]), .INPR_i(1'b0), .DR_i(DR[14]), .AC_i(AC[14]),
    .AC_i_1(AC[13]), .AC_i_1_2(AC[15]), .C_i(n1_bit_alu_14_c_i_1),
    .in_1({AND, ADD, DR_2, INPR_2, COM, SLR, SHL}));
  _1_bit_ALU u_1_bit_alu_16 (
    .C_i_1(Carry_E_t), .I_i(result[15]), .INPR_i(1'b0), .DR_i(DR[15]), .AC_i(AC[15]), .AC_i_1(AC[14]),
    .AC_i_1_2(E_IN), .C_i(n1_bit_alu_15_c_i_1), .in_1({AND, ADD, DR_2, INPR_2, COM, SLR, SHL}));

  // Other names for the same wires on the sheet: ctrl[6:0] = {AND, ADD, DR_2, INPR_2, COM, SLR, SHL}; SHR = SLR;
  //   IN0 = INPR[0]; IN1 = INPR[1]; IN2 = INPR[2]; IN3 = INPR[3]; IN4 = INPR[4]; IN5 = INPR[5]; IN6 = INPR[6];
  //   IN7 = INPR[7]; I0 = result[0]; I1 = result[1]; I2 = result[2]; I3 = result[3]; I4 = result[4]; I5 = result[5];
  //   I6 = result[6]; I7 = result[7]; I8 = result[8]; I9 = result[9]; I10 = result[10]; I11 = result[11];
  //   I12 = result[12]; I13 = result[13]; I14 = result[14]; I15 = result[15]
endmodule

module BUS (
  input  [15:0] NULL,
  input  [15:0] AR,
  input  [15:0] PC,
  input  [15:0] DR,
  input  [15:0] AC,
  input  [15:0] IR,
  input  [2:0] in_7,
  input  [15:0] TR,
  input  [15:0] MEMORY,
  output [15:0] out_10
);

  Multiplexer #(.select(3), .width(16), .enable("false")) multiplexer_1 (
    .in0(NULL), .in1(AR), .in2(PC), .in3(DR), .in4(AC), .in5(IR), .in6(TR), .in7(MEMORY), .out(out_10),
    .sel(in_7));
endmodule

module S (
  input  Clock,
  input  [3:0] T,
  input  [15:0] IR,
  input  I,
  output S
);

  wire and_1_out, D0, D1, D2, D3, D4, D5, D6, D7, not_1_out, r, T0, T1, T2, T3, T4, T5, T6, T7, T8, T9, T10,
       T11, T12, T13, T14, T15;

  Decoder #(.select(4), .enable("false")) decoder_1 (
    .out0(T0), .out1(T1), .out2(T2), .out3(T3), .out4(T4), .out5(T5), .out6(T6), .out7(T7), .out8(T8),
    .out9(T9), .out10(T10), .out11(T11), .out12(T12), .out13(T13), .out14(T14), .out15(T15), .sel(T));
  Decoder #(.select(3), .enable("false")) decoder_2 (
    .out0(D0), .out1(D1), .out2(D2), .out3(D3), .out4(D4), .out5(D5), .out6(D6), .out7(D7), .sel(IR[14:12]));
  and and_1 (and_1_out, r, IR[0]);
  J_K_Flip_Flop j_k_ff_1 (.J(and_1_out), .clk(Clock), .K(1'b0), .Q(S));  // open: Qn, preset, en, reset
  not not_1 (not_1_out, I);
  and and_2 (r, T3, D7, not_1_out);

  // Other names for the same wires on the sheet: B0 = IR[0]; B1 = IR[1]; B2 = IR[2]; B3 = IR[3]; B4 = IR[4];
  //   B5 = IR[5]; B6 = IR[6]; B7 = IR[7]; B8 = IR[8]; B9 = IR[9]; B10 = IR[10]; B11 = IR[11]
endmodule

module R (
  input  FGO,
  input  FGI,
  input  IEN,
  input  Clock,
  input  [3:0] in_5,
  output R
);

  wire and_1_out, and_2_out, nor_1_out, or_1_out, T0, T1, T2;

  Decoder #(.select(4), .enable("false")) decoder_1 (
    .out0(T0), .out1(T1), .out2(T2), .sel(in_5));  // open: out3, out4, out5, out6, out7, out8, out9, out10, out11, out12, out13, out14, out15
  or or_1 (or_1_out, FGO, FGI);
  nor nor_1 (nor_1_out, T0, T1, T2);
  and and_1 (and_1_out, or_1_out, IEN, nor_1_out);
  and and_2 (and_2_out, T2, R);
  J_K_Flip_Flop j_k_ff_1 (.J(and_1_out), .clk(Clock), .K(and_2_out), .Q(R));  // open: Qn, preset, en, reset
endmodule

module IEN (
  input  Clock,
  input  [3:0] T,
  input  R,
  input  [15:0] IR,
  input  I,
  output IEN
);

  wire and_1_out, and_2_out, and_3_out, D0, D1, D2, D3, D4, D5, D6, D7, not_1_out, or_1_out, p, r_t, T0, T1,
       T2, T3, T4, T5, T6, T7, T8, T9, T10, T11, T12, T13, T14, T15;

  Decoder #(.select(4), .enable("false")) decoder_1 (
    .out0(T0), .out1(T1), .out2(T2), .out3(T3), .out4(T4), .out5(T5), .out6(T6), .out7(T7), .out8(T8),
    .out9(T9), .out10(T10), .out11(T11), .out12(T12), .out13(T13), .out14(T14), .out15(T15), .sel(T));
  Decoder #(.select(3), .enable("false")) decoder_2 (
    .out0(D0), .out1(D1), .out2(D2), .out3(D3), .out4(D4), .out5(D5), .out6(D6), .out7(D7), .sel(IR[14:12]));
  and and_1 (and_1_out, R, T2);
  and and_2 (and_2_out, p, IR[6]);
  and and_3 (and_3_out, p, IR[7]);
  or or_1 (or_1_out, and_1_out, and_2_out);
  J_K_Flip_Flop j_k_ff_1 (.J(and_3_out), .clk(Clock), .K(or_1_out), .Q(IEN));  // open: Qn, preset, en, reset
  not not_1 (not_1_out, I);
  and and_4 (r_t, T3, D7, not_1_out);
  and and_5 (p, T3, D7, I);

  // Other names for the same wires on the sheet: B0 = IR[0]; B1 = IR[1]; B2 = IR[2]; B3 = IR[3]; B4 = IR[4];
  //   B5 = IR[5]; B6 = IR[6]; B7 = IR[7]; B8 = IR[8]; B9 = IR[9]; B10 = IR[10]; B11 = IR[11]
endmodule

module I (
  input  Clock,
  input  IR_15,
  input  [3:0] T,
  input  R,
  output I
);

  wire and_1_out, not_1_out, T0, T1, T2, T3, T4, T5, T6, T7, T8, T9, T10, T11, T12, T13, T14, T15;

  Decoder #(.select(4), .enable("false")) decoder_1 (
    .out0(T0), .out1(T1), .out2(T2), .out3(T3), .out4(T4), .out5(T5), .out6(T6), .out7(T7), .out8(T8),
    .out9(T9), .out10(T10), .out11(T11), .out12(T12), .out13(T13), .out14(T14), .out15(T15), .sel(T));
  not not_1 (not_1_out, R);
  and and_1 (and_1_out, not_1_out, T2);
  D_Flip_Flop d_ff_1 (.clk(Clock), .D(IR_15), .Q(I), .en(and_1_out));  // open: Qn, preset, reset
endmodule

module E (
  input  Clock,
  input  in_2,
  input  [3:0] T,
  input  R,
  input  I,
  input  [15:0] IR,
  output E
);

  wire and_1_out, and_2_out, and_3_out, and_4_out, D0, D1, D2, D3, D4, D5, D6, D7, not_1_out, not_2_out,
       not_3_out, or_1_out, or_2_out, or_3_out, p, r_t, T0, T1, T2, T3, T4, T5, T6, T7, T8, T9, T10, T11,
       T12, T13, T14, T15;

  Decoder #(.select(4), .enable("false")) decoder_1 (
    .out0(T0), .out1(T1), .out2(T2), .out3(T3), .out4(T4), .out5(T5), .out6(T6), .out7(T7), .out8(T8),
    .out9(T9), .out10(T10), .out11(T11), .out12(T12), .out13(T13), .out14(T14), .out15(T15), .sel(T));
  or or_1 (or_1_out, and_2_out, and_1_out);
  and and_1 (and_1_out, r_t, IR[8]);
  and and_2 (and_2_out, r_t, IR[10]);
  Decoder #(.select(3), .enable("false")) decoder_2 (
    .out0(D0), .out1(D1), .out2(D2), .out3(D3), .out4(D4), .out5(D5), .out6(D6), .out7(D7), .sel(IR[14:12]));
  not not_1 (not_1_out, or_1_out);
  not not_2 (not_2_out, in_2);
  and and_3 (and_3_out, in_2, not_1_out);
  and and_4 (and_4_out, not_2_out, not_1_out);
  or or_2 (or_2_out, and_3_out, and_1_out);
  or or_3 (or_3_out, and_4_out, and_1_out, and_2_out);
  J_K_Flip_Flop j_k_ff_1 (.J(or_2_out), .clk(Clock), .K(or_3_out), .Q(E));  // open: Qn, preset, en, reset
  not not_3 (not_3_out, I);
  and and_5 (r_t, T3, D7, not_3_out);
  and and_6 (p, T3, D7, I);

  // Other names for the same wires on the sheet: ALU_E_OUT = in_2; B0 = IR[0]; B1 = IR[1]; B2 = IR[2]; B3 = IR[3];
  //   B4 = IR[4]; B5 = IR[5]; B6 = IR[6]; B7 = IR[7]; B8 = IR[8]; B9 = IR[9]; B10 = IR[10]; B11 = IR[11]
endmodule

module FGI (
  input  Clock,
  input  [3:0] T,
  input  I,
  input  [15:0] IR,
  input  [7:0] INPR,
  output FGI
);

  wire and_1_out, D0, D1, D2, D3, D4, D5, D6, D7, not_1_out, OR_INPR, p, r, T0, T1, T2, T3, T4, T5, T6, T7,
       T8, T9, T10, T11, T12, T13, T14, T15;

  Decoder #(.select(4), .enable("false")) decoder_1 (
    .out0(T0), .out1(T1), .out2(T2), .out3(T3), .out4(T4), .out5(T5), .out6(T6), .out7(T7), .out8(T8),
    .out9(T9), .out10(T10), .out11(T11), .out12(T12), .out13(T13), .out14(T14), .out15(T15), .sel(T));
  Decoder #(.select(3), .enable("false")) decoder_2 (
    .out0(D0), .out1(D1), .out2(D2), .out3(D3), .out4(D4), .out5(D5), .out6(D6), .out7(D7), .sel(IR[14:12]));
  and and_1 (and_1_out, p, IR[11]);
  J_K_Flip_Flop j_k_ff_1 (.J(OR_INPR), .clk(Clock), .K(and_1_out), .Q(FGI));  // open: Qn, preset, en, reset
  not not_1 (not_1_out, I);
  and and_2 (r, T3, D7, not_1_out);
  and and_3 (p, T3, D7, I);
  or or_1 (OR_INPR, INPR[7], INPR[6], INPR[5], INPR[4], INPR[2], INPR[1], INPR[0], INPR[3]);

  // Other names for the same wires on the sheet: B0 = IR[0]; B1 = IR[1]; B2 = IR[2]; B3 = IR[3]; B4 = IR[4];
  //   B5 = IR[5]; B6 = IR[6]; B7 = IR[7]; B8 = IR[8]; B9 = IR[9]; B10 = IR[10]; B11 = IR[11]
endmodule

module FGO (
  input  Clock,
  input  [3:0] T,
  input  I,
  input  [15:0] IR,
  output FGO
);

  wire and_1_out, D0, D1, D2, D3, D4, D5, D6, D7, not_1_out, p, r, T0, T1, T2, T3, T4, T5, T6, T7, T8, T9,
       T10, T11, T12, T13, T14, T15;

  Decoder #(.select(4), .enable("false")) decoder_1 (
    .out0(T0), .out1(T1), .out2(T2), .out3(T3), .out4(T4), .out5(T5), .out6(T6), .out7(T7), .out8(T8),
    .out9(T9), .out10(T10), .out11(T11), .out12(T12), .out13(T13), .out14(T14), .out15(T15), .sel(T));
  Decoder #(.select(3), .enable("false")) decoder_2 (
    .out0(D0), .out1(D1), .out2(D2), .out3(D3), .out4(D4), .out5(D5), .out6(D6), .out7(D7), .sel(IR[14:12]));
  and and_1 (and_1_out, p, IR[10]);
  J_K_Flip_Flop j_k_ff_1 (.J(1'b0), .clk(Clock), .K(and_1_out), .Q(FGO));  // open: Qn, preset, en, reset
  not not_1 (not_1_out, I);
  and and_2 (r, T3, D7, not_1_out);
  and and_3 (p, T3, D7, I);

  // Other names for the same wires on the sheet: B0 = IR[0]; B1 = IR[1]; B2 = IR[2]; B3 = IR[3]; B4 = IR[4];
  //   B5 = IR[5]; B6 = IR[6]; B7 = IR[7]; B8 = IR[8]; B9 = IR[9]; B10 = IR[10]; B11 = IR[11]
endmodule

module AC (
  input  LD_AC,
  input  [15:0] INPUT,
  input  INR_AC,
  input  CLR_AC,
  input  Clock,
  output [15:0] OUTPUT
);

  Counter #(.width(16), .max('hffff)) counter_1 (
    .load(LD_AC), .D(INPUT), .count(INR_AC), .Q(OUTPUT), .clk(Clock), .clr(CLR_AC));  // open: carry
endmodule

module AR (
  input  LD_AR,
  input  [15:0] INPUT,
  input  CLR_AR,
  input  INR_AR,
  input  Clock,
  output [15:0] OUTPUT
);

  Counter #(.width(12), .max('hfff)) counter_1 (
    .load(LD_AR), .D(INPUT[11:0]), .count(INR_AR), .Q(OUTPUT[11:0]), .clk(Clock), .clr(CLR_AR));  // open: carry

  assign OUTPUT[15:12] = 4'b0000;
endmodule

module PC (
  input  LD_PC,
  input  [15:0] INPUT,
  input  CLR_PC,
  input  INR_PC,
  input  Clock,
  output [15:0] OUTPUT
);

  Counter #(.width(12), .max('hfff)) counter_1 (
    .load(LD_PC), .D(INPUT[11:0]), .count(INR_PC), .Q(OUTPUT[11:0]), .clk(Clock), .clr(CLR_PC));  // open: carry

  assign OUTPUT[15:12] = 4'b0000;
endmodule

module DR (
  input  LD_DR,
  input  [15:0] INPUT,
  input  INR_DR,
  input  CLR_DR,
  input  Clock,
  output [15:0] OUTPUT
);

  Counter #(.width(16), .max('hffff)) counter_1 (
    .load(LD_DR), .D(INPUT), .count(INR_DR), .Q(OUTPUT), .clk(Clock), .clr(CLR_DR));  // open: carry
endmodule

module IR (
  input  LD_IR,
  input  [15:0] INPUT,
  input  Clock,
  output [15:0] OUTPUT
);

  Counter #(.width(16), .max('hffff)) counter_1 (
    .load(LD_IR), .D(INPUT), .count(1'b0), .Q(OUTPUT), .clk(Clock));  // open: carry, clr
endmodule

module TR (
  input  LD_TR,
  input  [15:0] INPUT,
  input  CLR_TR,
  input  Clock,
  output [15:0] OUTPUT
);

  Counter #(.width(16), .max('hffff)) counter_1 (
    .load(LD_TR), .D(INPUT), .count(1'b0), .Q(OUTPUT), .clk(Clock), .clr(CLR_TR));  // open: carry
endmodule

module OUTR (
  input  LD_OUTR,
  input  [15:0] INPUT,
  input  Clock,
  output [7:0] OUTPUT
);

  Counter counter_1 (.load(LD_OUTR), .D(INPUT[7:0]), .count(1'b0), .Q(OUTPUT), .clk(Clock));  // open: carry, clr
endmodule

module INPR (
  output [7:0] out_1
);

  Register register_1 (.en(1'b0), .Q(out_1));  // open: D, clk, clr
endmodule

module BUS_control (
  input  [3:0] T,
  input  R,
  input  I,
  input  [15:0] IR,
  output [2:0] Select
);

  wire and_1_out, and_2_out, and_3_out, and_4_out, and_5_out, and_6_out, and_7_out, and_8_out, and_9_out,
       and_12_out, and_13_out, and_14_out, and_15_out, and_16_out, and_17_out, D0, D1, D2, D3, D4, D5, D6,
       D7, not_1_out, not_2_out, not_3_out, not_4_out, not_5_out, p, r_t, T0, T1, T2, T3, T4, T5, T6, T7, T8,
       T9, T10, T11, T12, T13, T14, T15, X1, X2, X3, X4, X5, X6, X7;

  and and_1 (and_1_out, T4, D4);
  and and_2 (and_2_out, T5, D5);
  not not_1 (not_1_out, R);
  and and_3 (and_3_out, not_1_out, T0);
  and and_4 (and_4_out, R, T0);
  and and_5 (and_5_out, T5, D2);
  and and_6 (and_6_out, T6, D6);
  and and_7 (and_7_out, T4, D3);
  and and_8 (and_8_out, p, IR[10]);
  Decoder #(.select(4), .enable("false")) decoder_1 (
    .out0(T0), .out1(T1), .out2(T2), .out3(T3), .out4(T4), .out5(T5), .out6(T6), .out7(T7), .out8(T8),
    .out9(T9), .out10(T10), .out11(T11), .out12(T12), .out13(T13), .out14(T14), .out15(T15), .sel(T));
  or or_1 (X1, and_1_out, and_2_out);
  and and_9 (and_9_out, T4, D5);
  or or_2 (X3, and_5_out, and_6_out);
  or or_3 (X4, and_7_out, and_8_out);
  Decoder #(.select(3), .enable("false")) decoder_2 (
    .out0(D0), .out1(D1), .out2(D2), .out3(D3), .out4(D4), .out5(D5), .out6(D6), .out7(D7), .sel(IR[14:12]));
  or or_4 (X2, and_3_out, and_9_out, and_4_out);
  not not_2 (not_2_out, R);
  and and_10 (X5, not_2_out, T2);
  and and_11 (X6, R, T1);
  not not_3 (not_3_out, R);
  not not_4 (not_4_out, D7);
  and and_12 (and_12_out, not_4_out, I, T3);
  and and_13 (and_13_out, not_3_out, T1);
  and and_14 (and_14_out, D0, T4);
  and and_15 (and_15_out, D1, T4);
  and and_16 (and_16_out, D2, T4);
  and and_17 (and_17_out, D6, T4);
  or or_5 (X7, and_13_out, and_14_out, and_15_out, and_12_out, and_16_out, and_17_out, r_t);
  not not_5 (not_5_out, I);
  and and_18 (r_t, T3, D7, not_5_out);
  and and_19 (p, T3, D7, I);
  Priority_Encoder priority_encoder_1 (
    .in0(1'b0), .in1(X1), .in2(X2), .in3(X3), .in4(X4), .in5(X5), .in6(X6), .in7(X7), .out(Select));  // open: en_in, gs, en_out

  // Other names for the same wires on the sheet: B0 = IR[0]; B1 = IR[1]; B2 = IR[2]; B3 = IR[3]; B4 = IR[4];
  //   B5 = IR[5]; B6 = IR[6]; B7 = IR[7]; B8 = IR[8]; B9 = IR[9]; B10 = IR[10]; B11 = IR[11]
endmodule

module AR_control (
  input  [3:0] T,
  input  R,
  input  I,
  input  [15:0] IR,
  output LD_AR,
  output CLR_AR,
  output INR_AR
);

  wire and_1_out, and_2_out, and_3_out, D0, D1, D2, D3, D4, D5, D6, D7, not_1_out, not_2_out, not_3_out,
       not_4_out, p, r_t, T0, T1, T2, T3, T4, T5, T6, T7, T8, T9, T10, T11, T12, T13, T14, T15;

  Decoder #(.select(4), .enable("false")) decoder_1 (
    .out0(T0), .out1(T1), .out2(T2), .out3(T3), .out4(T4), .out5(T5), .out6(T6), .out7(T7), .out8(T8),
    .out9(T9), .out10(T10), .out11(T11), .out12(T12), .out13(T13), .out14(T14), .out15(T15), .sel(T));
  not not_1 (not_1_out, R);
  not not_2 (not_2_out, R);
  not not_3 (not_3_out, D7);
  Decoder #(.select(3), .enable("false")) decoder_2 (
    .out0(D0), .out1(D1), .out2(D2), .out3(D3), .out4(D4), .out5(D5), .out6(D6), .out7(D7), .sel(IR[14:12]));
  and and_1 (and_1_out, T0, not_1_out);
  and and_2 (and_2_out, T2, not_2_out);
  and and_3 (and_3_out, I, T3, not_3_out);
  and and_4 (CLR_AR, R, T0);
  and and_5 (INR_AR, D5, T4);
  or or_1 (LD_AR, and_1_out, and_2_out, and_3_out);
  not not_4 (not_4_out, I);
  and and_6 (r_t, T3, D7, not_4_out);
  and and_7 (p, T3, D7, I);

  // Other names for the same wires on the sheet: B0 = IR[0]; B1 = IR[1]; B2 = IR[2]; B3 = IR[3]; B4 = IR[4];
  //   B5 = IR[5]; B6 = IR[6]; B7 = IR[7]; B8 = IR[8]; B9 = IR[9]; B10 = IR[10]; B11 = IR[11]
endmodule

module PC_control (
  input  [3:0] T,
  input  [15:0] AC,
  input  [15:0] IR,
  input  I,
  input  R,
  input  [15:0] DR,
  input  E,
  input  FGI,
  input  FGO,
  output INR_PC,
  output CLR_PC,
  output LD_PC
);

  wire and_2_out, and_3_out, and_4_out, and_5_out, and_6_out, and_7_out, and_8_out, and_9_out, and_10_out,
       and_11_out, and_12_out, D0, D1, D2, D3, D4, D5, D6, D7, not_1_out, not_2_out, not_3_out, not_4_out,
       not_5_out, not_6_out, OR_AC, OR_DR, p, r_t, T0, T1, T2, T3, T4, T5, T6, T7, T8, T9, T10, T11, T12,
       T13, T14, T15;

  Decoder #(.select(4), .enable("false")) decoder_1 (
    .out0(T0), .out1(T1), .out2(T2), .out3(T3), .out4(T4), .out5(T5), .out6(T6), .out7(T7), .out8(T8),
    .out9(T9), .out10(T10), .out11(T11), .out12(T12), .out13(T13), .out14(T14), .out15(T15), .sel(T));
  Decoder #(.select(3), .enable("false")) decoder_2 (
    .out0(D0), .out1(D1), .out2(D2), .out3(D3), .out4(D4), .out5(D5), .out6(D6), .out7(D7), .sel(IR[14:12]));
  not not_1 (not_1_out, OR_AC);
  not not_2 (not_2_out, R);
  not not_3 (not_3_out, OR_DR);
  not not_4 (not_4_out, AC[15]);
  not not_5 (not_5_out, E);
  and and_1 (CLR_PC, R, T1);
  and and_2 (and_2_out, D4, T4);
  and and_3 (and_3_out, D5, T5);
  and and_4 (and_4_out, not_2_out, T1);
  and and_5 (and_5_out, R, T2);
  and and_6 (and_6_out, D6, T6, not_3_out);
  and and_7 (and_7_out, r_t, IR[4], not_4_out);
  and and_8 (and_8_out, r_t, IR[3], AC[15]);
  and and_9 (and_9_out, r_t, IR[2], not_1_out);
  and and_10 (and_10_out, r_t, IR[1], not_5_out);
  and and_11 (and_11_out, p, IR[9], FGI);
  and and_12 (and_12_out, p, FGO);
  or or_1 (LD_PC, and_2_out, and_3_out);
  or or_2 (INR_PC, and_4_out, and_5_out, and_6_out, and_7_out, and_8_out, and_9_out, and_10_out, and_11_out, and_12_out);
  not not_6 (not_6_out, I);
  and and_13 (r_t, T3, D7, not_6_out);
  and and_14 (p, T3, D7, I);
  or or_3 (OR_AC, AC[15], AC[14], AC[13], AC[12], AC[11], AC[10], AC[9], AC[8], AC[6], AC[5], AC[4], AC[3], AC[2], AC[1], AC[0], AC[7]);
  or or_4 (OR_DR, DR[15], DR[14], DR[13], DR[12], DR[11], DR[10], DR[9], DR[8], DR[6], DR[5], DR[4], DR[3], DR[2], DR[1], DR[0], DR[7]);

  // Other names for the same wires on the sheet: B0 = IR[0]; B1 = IR[1]; B2 = IR[2]; B3 = IR[3]; B4 = IR[4];
  //   B5 = IR[5]; B6 = IR[6]; B7 = IR[7]; B8 = IR[8]; B9 = IR[9]; B10 = IR[10]; B11 = IR[11]
endmodule

module DR_control (
  input  [3:0] T,
  input  R,
  input  I,
  input  [15:0] IR,
  output LD_DR,
  output INR_DR
);

  wire and_1_out, and_2_out, and_3_out, and_4_out, D0, D1, D2, D3, D4, D5, D6, D7, not_1_out, p, r_t, T0, T1,
       T2, T3, T4, T5, T6, T7, T8, T9, T10, T11, T12, T13, T14, T15;

  Decoder #(.select(4), .enable("false")) decoder_1 (
    .out0(T0), .out1(T1), .out2(T2), .out3(T3), .out4(T4), .out5(T5), .out6(T6), .out7(T7), .out8(T8),
    .out9(T9), .out10(T10), .out11(T11), .out12(T12), .out13(T13), .out14(T14), .out15(T15), .sel(T));
  Decoder #(.select(3), .enable("false")) decoder_2 (
    .out0(D0), .out1(D1), .out2(D2), .out3(D3), .out4(D4), .out5(D5), .out6(D6), .out7(D7), .sel(IR[14:12]));
  and and_1 (and_1_out, D0, T4);
  and and_2 (and_2_out, D1, T4);
  and and_3 (and_3_out, D2, T4);
  and and_4 (and_4_out, D6, T4);
  and and_5 (INR_DR, D6, T5);
  or or_1 (LD_DR, and_1_out, and_2_out, and_3_out, and_4_out);
  not not_1 (not_1_out, I);
  and and_6 (r_t, T3, D7, not_1_out);
  and and_7 (p, T3, D7, I);

  // Other names for the same wires on the sheet: B0 = IR[0]; B1 = IR[1]; B2 = IR[2]; B3 = IR[3]; B4 = IR[4];
  //   B5 = IR[5]; B6 = IR[6]; B7 = IR[7]; B8 = IR[8]; B9 = IR[9]; B10 = IR[10]; B11 = IR[11]
endmodule

module AC_control (
  input  [3:0] T,
  input  I,
  input  [15:0] IR,
  output LD_AC,
  output [6:0] CTRL,
  output INR_AC,
  output CLR_AC
);

  wire ADD_out, AND_out, COM_out, D0, D1, D2, D3, D4, D5, D6, D7, DR_out, INPR_out, not_1_out, p, r, SHL_out,
       SHR_out, T0, T1, T2, T3, T4, T5, T6, T7, T8, T9, T10, T11, T12, T13, T14, T15;

  Decoder #(.select(4), .enable("false")) decoder_1 (
    .out0(T0), .out1(T1), .out2(T2), .out3(T3), .out4(T4), .out5(T5), .out6(T6), .out7(T7), .out8(T8),
    .out9(T9), .out10(T10), .out11(T11), .out12(T12), .out13(T13), .out14(T14), .out15(T15), .sel(T));
  and AND (AND_out, D0, T5);
  and ADD (ADD_out, T5, D1);
  and DR (DR_out, T5, D2);
  and INPR (INPR_out, p, IR[11]);
  and COM (COM_out, r, IR[9]);
  and SHR (SHR_out, r, IR[7]);
  and SHL (SHL_out, r, IR[6]);
  and INC (INR_AC, r, IR[5]);
  and CLR (CLR_AC, r, IR[11]);
  Decoder #(.select(3), .enable("false")) decoder_2 (
    .out0(D0), .out1(D1), .out2(D2), .out3(D3), .out4(D4), .out5(D5), .out6(D6), .out7(D7), .sel(IR[14:12]));
  or or_1 (LD_AC, AND_out, ADD_out, DR_out, INPR_out, COM_out, SHR_out, SHL_out);
  and AND_2 (CTRL[0], D0, T5);
  and ADD_2 (CTRL[1], T5, D1);
  and DR_2 (CTRL[2], T5, D2);
  and INPR_2 (CTRL[3], p, IR[11]);
  and COM_2 (CTRL[4], r, IR[9]);
  and SHR_2 (CTRL[5], r, IR[7]);
  and SHL_2 (CTRL[6], r, IR[6]);
  not not_1 (not_1_out, I);
  and and_3 (r, T3, D7, not_1_out);
  and and_4 (p, T3, D7, I);

  // Other names for the same wires on the sheet: B0 = IR[0]; B1 = IR[1]; B2 = IR[2]; B3 = IR[3]; B4 = IR[4];
  //   B5 = IR[5]; B6 = IR[6]; B7 = IR[7]; B8 = IR[8]; B9 = IR[9]; B10 = IR[10]; B11 = IR[11]
endmodule

module IR_control (
  input  [3:0] T,
  input  R,
  output LD_IR
);

  wire not_1_out, T0, T1, T2, T3, T4, T5, T6, T7, T8, T9, T10, T11, T12, T13, T14, T15;

  Decoder #(.select(4), .enable("false")) decoder_1 (
    .out0(T0), .out1(T1), .out2(T2), .out3(T3), .out4(T4), .out5(T5), .out6(T6), .out7(T7), .out8(T8),
    .out9(T9), .out10(T10), .out11(T11), .out12(T12), .out13(T13), .out14(T14), .out15(T15), .sel(T));
  not not_1 (not_1_out, R);
  and and_1 (LD_IR, not_1_out, T1);
endmodule

module TR_control (
  input  [3:0] T,
  input  R,
  output LD_TR
);

  wire T0, T1, T2, T3, T4, T5, T6, T7, T8, T9, T10, T11, T12, T13, T14, T15;

  Decoder #(.select(4), .enable("false")) decoder_1 (
    .out0(T0), .out1(T1), .out2(T2), .out3(T3), .out4(T4), .out5(T5), .out6(T6), .out7(T7), .out8(T8),
    .out9(T9), .out10(T10), .out11(T11), .out12(T12), .out13(T13), .out14(T14), .out15(T15), .sel(T));
  and and_1 (LD_TR, R, T0);
endmodule

module OUTR_control (
  input  [3:0] T,
  input  [15:0] IR,
  input  I,
  output LD_OUTR
);

  wire D0, D1, D2, D3, D4, D5, D6, D7, p, T0, T1, T2, T3, T4, T5, T6, T7, T8, T9, T10, T11, T12, T13, T14,
       T15;

  Decoder #(.select(4), .enable("false")) decoder_1 (
    .out0(T0), .out1(T1), .out2(T2), .out3(T3), .out4(T4), .out5(T5), .out6(T6), .out7(T7), .out8(T8),
    .out9(T9), .out10(T10), .out11(T11), .out12(T12), .out13(T13), .out14(T14), .out15(T15), .sel(T));
  Decoder #(.select(3), .enable("false")) decoder_2 (
    .out0(D0), .out1(D1), .out2(D2), .out3(D3), .out4(D4), .out5(D5), .out6(D6), .out7(D7), .sel(IR[14:12]));
  and and_1 (LD_OUTR, p, IR[10]);
  and and_2 (p, T3, D7, I);

  // Other names for the same wires on the sheet: B0 = IR[0]; B1 = IR[1]; B2 = IR[2]; B3 = IR[3]; B4 = IR[4];
  //   B5 = IR[5]; B6 = IR[6]; B7 = IR[7]; B8 = IR[8]; B9 = IR[9]; B10 = IR[10]; B11 = IR[11]
endmodule

module MEMORY_control (
  input  [3:0] T,
  input  R,
  input  I,
  input  [15:0] IR,
  output WR_MEMORY,
  output RD_MEMORY
);

  wire and_1_out, and_2_out, and_3_out, and_4_out, and_5_out, and_6_out, and_7_out, and_8_out, and_9_out,
       and_10_out, D0, D1, D2, D3, D4, D5, D6, D7, not_1_out, not_2_out, T0, T1, T2, T3, T4, T5, T6, T7, T8,
       T9, T10, T11, T12, T13, T14, T15;

  Decoder #(.select(4), .enable("false")) decoder_1 (
    .out0(T0), .out1(T1), .out2(T2), .out3(T3), .out4(T4), .out5(T5), .out6(T6), .out7(T7), .out8(T8),
    .out9(T9), .out10(T10), .out11(T11), .out12(T12), .out13(T13), .out14(T14), .out15(T15), .sel(T));
  and and_1 (and_1_out, R, T1);
  and and_2 (and_2_out, D3, T4);
  and and_3 (and_3_out, D5, T4);
  and and_4 (and_4_out, D6, T6);
  Decoder #(.select(3), .enable("false")) decoder_2 (
    .out0(D0), .out1(D1), .out2(D2), .out3(D3), .out4(D4), .out5(D5), .out6(D6), .out7(D7), .sel(IR[14:12]));
  or or_1 (WR_MEMORY, and_1_out, and_2_out, and_3_out, and_4_out);
  not not_1 (not_1_out, R);
  not not_2 (not_2_out, D7);
  and and_5 (and_5_out, not_1_out, T1);
  and and_6 (and_6_out, D0, T4);
  and and_7 (and_7_out, D1, T4);
  and and_8 (and_8_out, D2, T4);
  and and_9 (and_9_out, I, not_2_out, T3);
  and and_10 (and_10_out, D6, T4);
  or or_2 (RD_MEMORY, and_5_out, and_6_out, and_7_out, and_8_out, and_9_out, and_10_out);

  // Other names for the same wires on the sheet: B0 = IR[0]; B1 = IR[1]; B2 = IR[2]; B3 = IR[3]; B4 = IR[4];
  //   B5 = IR[5]; B6 = IR[6]; B7 = IR[7]; B8 = IR[8]; B9 = IR[9]; B10 = IR[10]; B11 = IR[11]
endmodule

module SC_control (
  input  [3:0] T,
  input  R,
  input  I,
  input  [15:0] IR,
  output CLR_SC
);

  wire and_1_out, and_2_out, and_3_out, and_4_out, and_5_out, and_6_out, and_7_out, and_8_out, D0, D1, D2,
       D3, D4, D5, D6, D7, not_1_out, p, r_t, T0, T1, T2, T3, T4, T5, T6, T7, T8, T9, T10, T11, T12, T13,
       T14, T15;

  Decoder #(.select(4), .enable("false")) decoder_1 (
    .out0(T0), .out1(T1), .out2(T2), .out3(T3), .out4(T4), .out5(T5), .out6(T6), .out7(T7), .out8(T8),
    .out9(T9), .out10(T10), .out11(T11), .out12(T12), .out13(T13), .out14(T14), .out15(T15), .sel(T));
  Decoder #(.select(3), .enable("false")) decoder_2 (
    .out0(D0), .out1(D1), .out2(D2), .out3(D3), .out4(D4), .out5(D5), .out6(D6), .out7(D7), .sel(IR[14:12]));
  and and_1 (and_1_out, R, T2);
  and and_2 (and_2_out, D0, T5);
  and and_3 (and_3_out, D1, T5);
  and and_4 (and_4_out, D2, T5);
  and and_5 (and_5_out, D3, T4);
  and and_6 (and_6_out, D4, T4);
  and and_7 (and_7_out, D5, T5);
  and and_8 (and_8_out, D6, T6);
  or or_1 (CLR_SC, and_1_out, and_2_out, and_3_out, and_4_out, and_5_out, and_6_out, and_7_out, and_8_out, r_t, p);
  not not_1 (not_1_out, I);
  and and_9 (r_t, T3, D7, not_1_out);
  and and_10 (p, T3, D7, I);

  // Other names for the same wires on the sheet: B0 = IR[0]; B1 = IR[1]; B2 = IR[2]; B3 = IR[3]; B4 = IR[4];
  //   B5 = IR[5]; B6 = IR[6]; B7 = IR[7]; B8 = IR[8]; B9 = IR[9]; B10 = IR[10]; B11 = IR[11]
endmodule
